# Fritzing sketch esp_linky (saved by Fritzing 0.9.3b)

parts:
  U1 = ESP8266 WiFi Module [part_number=ESP8266]
  R1 = Resistor [tolerance=±5% resistance=10k package="0603 [SMD]"]  # not connected
  R2 = Resistor [tolerance=±5% resistance=10k package="0603 [SMD]"]
  R3 = Resistor [tolerance=±5% resistance=1k package="0603 [SMD]"]
  Q1 = MOSFET-NCHANNEL [package=to-92]
  Power_plug1 = Power plug
  U2 = Mini-360 DC-DC Buck converter [package=THT]
  OC1 = LiteOn LTV-819-2 [part_number=LTV-819-2 package="THT DIP-4"]

nets:
  N1: U1.RXD, Q1.S
  N2: U1.VCC, U2.OUT+, OC1.Pin_4
  N3: U1.GND, U2.OUT-
  N4: R2.Pin_0, Q1.G, OC1.Pin_3
  N5: R3.Pin_1, OC1.Pin_2
  N6: Power_plug1.GND, U2.IN-
  N7: Power_plug1.VCC, U2.IN+

notes:
  ESP8266 (ESP01S) + ESPHOME / HA
  5V
  linky 1
  linky 2
  XL6009 5v=> 3.3v
  BS170
  LTV814
  1K Linky (4.7k ancien compteur)
  10K

custom parts:
  ESP8266 WiFi Module: Generic WiFi Module based on the ESP8266 with onboard PCB antenna and UART communications
  MOSFET-NCHANNEL: Generic NMOS footprint
  Mini-360 DC-DC Buck converter: Mini-360 DC-DC Buck converter. Tiny buck step down voltage converter, input voltage 4.75 to 23V output 1 to 17V adjustable. Available from ebay and the like.
  LiteOn LTV-819-2: Optocoupler
